// Logisim project ceepoo.circ as structural Verilog: 16 circuits, main circuit registre
module bboard_8 (
  input  [7:0] in_1,
  input  in_2,
  input  in_3
);

  wire clock_1_out, n8cc_1_bus1, n8cc_1_flags_2, n8cc_1_ir_2, n8cc_1_mar, n8cc_1_tmp;
  wire [1:0] n8cc_1_acc_2, n8cc_1_iar, n8cc_1_r0, n8cc_1_r1, n8cc_1_r2, n8cc_1_r3, n8cc_1_ram;
  wire [2:0] n8cc_1_op_code;
  wire [3:0] alu_1_cout, register_3_q;
  wire [7:0] alu_1_acc_0, bus1_1_buso, controlled_buffer_1_out, MAR_q, register_1_q, register_2_q,
       register_4_q, registre_1_out_4, registre_2_out_4, registre_3_out_4, registre_4_out_4,
       registre_5_out_4, registre_6_out_4;

  Register register_1 (.D(in_1), .Q(register_1_q), .clk(in_2));  // open: en, clr
  Clock clock_1 (.out(clock_1_out));
  assign controlled_buffer_1_out = in_3 ? register_1_q : 8'bz;  // Controlled_Buffer controlled_buffer_1
  registre registre_1 (
    .I(controlled_buffer_1_out), .s_e(n8cc_1_r3), .O(controlled_buffer_1_out), .out_4(registre_1_out_4));  // open: in_2
  // Probe on registre_1_out_4
  Register register_2 (.D(controlled_buffer_1_out), .Q(register_2_q), .clk(n8cc_1_ir_2));  // open: en, clr
  registre registre_2 (
    .I(controlled_buffer_1_out), .s_e(n8cc_1_iar), .O(controlled_buffer_1_out), .out_4(registre_2_out_4));  // open: in_2
  // Probe on registre_2_out_4
  registre registre_3 (
    .I(controlled_buffer_1_out), .s_e(n8cc_1_r0), .O(controlled_buffer_1_out), .out_4(registre_3_out_4));  // open: in_2
  registre registre_4 (
    .I(controlled_buffer_1_out), .s_e(n8cc_1_r2), .O(controlled_buffer_1_out), .out_4(registre_4_out_4));  // open: in_2
  registre registre_5 (
    .I(controlled_buffer_1_out), .s_e(n8cc_1_r1), .O(controlled_buffer_1_out), .out_4(registre_5_out_4));  // open: in_2
  // Probe on registre_3_out_4
  // Probe on registre_5_out_4
  // Probe on registre_4_out_4
  _8CC u_8cc_1 (
    .bus1(n8cc_1_bus1), .RAM(n8cc_1_ram[0]), .ACC_2(n8cc_1_acc_2[0]), .IAR(n8cc_1_iar[0]), .R0(n8cc_1_r0[0]),
    .R1(n8cc_1_r1[0]), .OP_CODE(n8cc_1_op_code), .MAR(n8cc_1_mar), .ACC(n8cc_1_acc_2[1]),
    .RAM_2(n8cc_1_ram[1]), .TMP(n8cc_1_tmp), .IR_2(n8cc_1_ir_2), .IAR_2(n8cc_1_iar[1]), .IR(register_2_q),
    .R2(n8cc_1_r2[0]), .R3(n8cc_1_r3[0]), .R0_2(n8cc_1_r0[1]), .R1_2(n8cc_1_r1[1]), .R2_2(n8cc_1_r2[1]),
    .R3_2(n8cc_1_r3[1]), .FLAGS_2(n8cc_1_flags_2), .FLAGS(register_3_q), .CLK_IN(clock_1_out));
  // Probe on controlled_buffer_1_out
  // Probe on controlled_buffer_1_out
  // Probe on controlled_buffer_1_out
  // Probe on controlled_buffer_1_out
  Register MAR (.D(controlled_buffer_1_out), .Q(MAR_q), .clk(n8cc_1_mar));  // open: en, clr
  Register #(.width(4)) register_3 (.D(alu_1_cout), .Q(register_3_q), .clk(n8cc_1_flags_2));  // open: en, clr
  RAM ram_1 (.addr(MAR_q), .data(controlled_buffer_1_out), .clk(n8cc_1_ram[1]), .ld(n8cc_1_ram[0]));  // open: sel, clr
  Register register_4 (.D(controlled_buffer_1_out), .Q(register_4_q), .clk(n8cc_1_tmp));  // open: en, clr
  bus1 bus1_1 (.OP(n8cc_1_bus1), .BUSI(register_4_q), .BUSO(bus1_1_buso));
  ALU alu_1 (
    .cin(register_3_q[0]), .op(n8cc_1_op_code), .zero(alu_1_cout[3]), .acc_0(alu_1_acc_0),
    .cout(alu_1_cout[0]), .a_larger(alu_1_cout[1]), .eq(alu_1_cout[2]), .a(controlled_buffer_1_out),
    .b(bus1_1_buso));
  registre registre_6 (
    .I(alu_1_acc_0), .s_e(n8cc_1_acc_2), .O(controlled_buffer_1_out), .out_4(registre_6_out_4));  // open: in_2
  // Probe on registre_6_out_4
  // Probe on controlled_buffer_1_out
  // Probe on bus1_1_buso
endmodule

module bboard_16 (
  input  [7:0] in_1,
  input  [1:0] in_2,
  input  str,
  input  ld,
  input  _0,
  input  [1:0] regsel,
  input  S_CNTR,
  input  E_CNTR_plus_plus,
  input  wipe,
  input  _8sa,
  input  tmp0,
  input  tmp1,
  input  _16sa,
  input  tmpset,
  input  OP,
  input  acc1sel,
  input  [2:0] in_17,
  input  [1:0] in_18
);

  wire or_1_out, undriven_2;
  wire [1:0] ccircuitwrapper16_1_rs_e, ccircuitwrapper16_1_rsel_a, ccircuitwrapper16_1_rsel_b,
       demultiplexer_1_out0, demultiplexer_1_out1, demultiplexer_1_out2, demultiplexer_1_out3, undriven;
  wire [7:0] _8_MAR_q, alu_1_p4, alu_1_p5, register_1_q, register_3_q, register_4_q, registre_1_out_4,
       registre_2_out_4, registre_3_out_4, registre_4_out_4, registre_5_out_4, registre_6_out_4,
       registre_7_out_4, registre_8_out_4;
  wire [15:0] counter_1_q, register_2_q;
  wire [15:8] registre_1_o;

  // Probe on in_1
  registre registre_1 (.I(in_1), .s_e(in_2), .O(registre_1_o), .out_4(registre_1_out_4));  // open: in_2
  // Probe on registre_1_out_4
  Demultiplexer #(.select(2), .width(2)) demultiplexer_1 (
    .out0(demultiplexer_1_out0), .out1(demultiplexer_1_out1), .out2(demultiplexer_1_out2),
    .out3(demultiplexer_1_out3), .in(undriven), .sel(regsel));  // open: en
  registre registre_2 (
    .I(registre_1_o), .s_e(demultiplexer_1_out2), .O(registre_1_o), .out_4(registre_2_out_4), .in_2(wipe));
  registre registre_3 (
    .I(registre_1_o), .s_e(demultiplexer_1_out0), .O(registre_1_o), .out_4(registre_3_out_4), .in_2(wipe));
  registre registre_4 (
    .I(registre_1_o), .s_e(demultiplexer_1_out1), .O(registre_1_o), .out_4(registre_4_out_4), .in_2(wipe));
  // Probe on registre_4_out_4
  // Probe on registre_3_out_4
  // Probe on registre_2_out_4
  Register IR (.D(registre_1_o), .clk(undriven_2));  // open: en, Q, clr
  registre registre_5 (
    .I(registre_1_o), .s_e(demultiplexer_1_out3), .O(registre_1_o), .out_4(registre_5_out_4), .in_2(wipe));
  // Probe on registre_5_out_4
  registre registre_6 (.I(registre_1_o), .O(registre_1_o), .out_4(registre_6_out_4));  // open: s_e, in_2
  // Probe on registre_6_out_4
  ccircuitwrapper16 ccircuitwrapper16_1 (
    .RS_E(ccircuitwrapper16_1_rs_e), .RSEL_A(ccircuitwrapper16_1_rsel_a), .RSEL_B(ccircuitwrapper16_1_rsel_b));  // open: SET_8_MAR, SET_16_MAR, SET_RAM, SET_TMP, BUS_1, IAR0, IAR1, SET_ALU_ACC1, SET_IR, EN_RAM, SET_OP, ACC0, IR, out_12, out_14, out_16
  registre registre_7 (.I(registre_1_o), .O(registre_1_o), .out_4(registre_7_out_4));  // open: s_e, in_2
  // Probe on registre_7_out_4
  Register _8_MAR (.D(registre_1_o), .Q(_8_MAR_q), .clk(_8sa));  // open: en, clr
  // Probe on registre_1_o
  // Probe on registre_1_o
  // Probe on registre_1_o
  // Probe on registre_1_o
  // Probe on {registre_1_o, _8_MAR_q}
  or or_1 (or_1_out, S_CNTR, E_CNTR_plus_plus);
  Register register_1 (.D(registre_1_o), .Q(register_1_q), .clk(tmpset));  // open: en, clr
  // ALU alu_1: pin names not known; wires that end beside it: in_17, acc1sel, registre_1_o, alu_1_p4, alu_1_p5
  Register #(.width(16)) register_2 (
    .D({registre_1_o, _8_MAR_q}), .Q(register_2_q), .clk(_16sa), .clr(_0));  // open: en
  Counter #(.width(16), .max('hffff)) counter_1 (
    .load(S_CNTR), .D({registre_1_o, _8_MAR_q}), .count(E_CNTR_plus_plus), .Q(counter_1_q), .clk(or_1_out));  // open: carry, clr
  bus1 bus1_1 (.OP(OP), .BUSI(register_1_q), .BUSO(alu_1_p5));
  // Probe on alu_1_p5
  registre registre_8 (.I(alu_1_p4), .s_e(in_18), .O(registre_1_o), .out_4(registre_8_out_4));  // open: in_2
  // Probe on registre_8_out_4
  RAM #(.addrWidth(16)) ram_1 (.addr(register_2_q), .data(registre_1_o), .clk(str), .ld(ld));  // open: sel, clr
  assign registre_1_o = tmp1 ? register_3_q : 8'bz;  // Controlled_Buffer controlled_buffer_1
  Register register_3 (.D(counter_1_q[7:0]), .Q(register_3_q));  // open: en, clk, clr
  assign registre_1_o = tmp0 ? register_4_q : 8'bz;  // Controlled_Buffer controlled_buffer_2
  Register register_4 (.D(counter_1_q[15:8]), .Q(register_4_q));  // open: en, clk, clr
endmodule

module registre (
  input  [7:0] I,
  input  in_2,
  input  [1:0] s_e,
  output [7:0] out_4,
  output [7:0] O
);

  assign O = s_e[0] ? out_4 : 8'bz;  // Controlled_Buffer controlled_buffer_1
  Register register_1 (.D(I), .Q(out_4), .clk(s_e[1]), .clr(in_2));  // open: en
  Pull_Resistor pull_resistor_1 (.node(s_e[0]));
endmodule

module ALU (
  input  [7:0] a,
  input  [7:0] b,
  input  cin,
  input  [2:0] op,
  output zero,
  output [7:0] acc_0,
  output cout,
  output a_larger,
  output eq
);

  wire adder_1_cout, decoder_1_out0, decoder_1_out1, decoder_1_out2, decoder_1_out3, decoder_1_out4,
       decoder_1_out5, decoder_1_out6, or_2_out, sh_l_1_cout, sh_r_1_cout;
  wire [7:0] adder_1_out, and_1_out, buffer_1_out, not_1_out, or_1_out, sh_l_1_out_3, sh_r_1_out_4, xor_1_out;

  assign not_1_out = ~a;  // NOT_Gate not_1, 8 bits wide
  Comparator #(.mode("unsigned")) comparator_1 (.a(a), .b(b), .gt(a_larger), .eq(eq));  // open: lt
  assign xor_1_out = a ^ b;  // XOR_Gate xor_1, 8 bits wide
  assign or_1_out = a | b;  // OR_Gate or_1, 8 bits wide
  assign and_1_out = a & b;  // AND_Gate and_1, 8 bits wide
  sh_l sh_l_1 (.in_2(a), .out_3(sh_l_1_out_3), .cin(cin), .cout(sh_l_1_cout));
  assign acc_0 = decoder_1_out2 ? sh_l_1_out_3 : 8'bz;  // Controlled_Buffer controlled_buffer_1
  assign cout = decoder_1_out2 ? sh_l_1_cout : 1'bz;  // Controlled_Buffer controlled_buffer_2
  assign cout = decoder_1_out1 ? sh_r_1_cout : 1'bz;  // Controlled_Buffer controlled_buffer_3
  sh_r sh_r_1 (.in_1(a), .out_4(sh_r_1_out_4), .cout(sh_r_1_cout), .cin(cin));
  assign acc_0 = decoder_1_out1 ? sh_r_1_out_4 : 8'bz;  // Controlled_Buffer controlled_buffer_4
  assign acc_0 = decoder_1_out0 ? adder_1_out : 8'bz;  // Controlled_Buffer controlled_buffer_5
  Adder adder_1 (.a(a), .b(b), .out(adder_1_out), .cin(cin), .cout(adder_1_cout));
  assign cout = decoder_1_out0 ? adder_1_cout : 1'bz;  // Controlled_Buffer controlled_buffer_6
  Decoder #(.select(3)) decoder_1 (
    .out0(decoder_1_out0), .out1(decoder_1_out1), .out2(decoder_1_out2), .out3(decoder_1_out3),
    .out4(decoder_1_out4), .out5(decoder_1_out5), .out6(decoder_1_out6), .sel(op));  // open: out7, en
  assign acc_0 = decoder_1_out6 ? xor_1_out : 8'bz;  // Controlled_Buffer controlled_buffer_7
  assign acc_0 = decoder_1_out5 ? or_1_out : 8'bz;  // Controlled_Buffer controlled_buffer_8
  assign acc_0 = decoder_1_out4 ? and_1_out : 8'bz;  // Controlled_Buffer controlled_buffer_9
  assign acc_0 = decoder_1_out3 ? not_1_out : 8'bz;  // Controlled_Buffer controlled_buffer_10
  assign buffer_1_out = acc_0;  // Buffer buffer_1, 8 bits wide
  Pull_Resistor pull_resistor_1 (.node(buffer_1_out));
  or or_2 (or_2_out, buffer_1_out[0], buffer_1_out[1], buffer_1_out[2], buffer_1_out[3], buffer_1_out[4], buffer_1_out[5], buffer_1_out[6], buffer_1_out[7]);
  not not_2 (zero, or_2_out);
endmodule

module sh_l (
  input  cin,
  input  [7:0] in_2,
  output [7:0] out_3,
  output cout
);


  assign cout = in_2[7];
  assign out_3 = {in_2[6:0], cin};
endmodule

module sh_r (
  input  [7:0] in_1,
  input  cin,
  output cout,
  output [7:0] out_4
);


  assign cout = in_1[0];
  assign out_4 = {cin, in_1[7:1]};
endmodule

module clock (
  input  in_1,
  output clk,
  output clk_e,
  output clk_s
);

  wire counter_2_q, not_1_out;

  Counter #(.width(1), .max('h1)) counter_1 (.Q(clk), .clk(in_1));  // open: load, D, count, carry, clr
  Counter #(.width(1), .max('h1)) counter_2 (.Q(counter_2_q), .clk(not_1_out));  // open: load, D, count, carry, clr
  not not_1 (not_1_out, in_1);
  or or_1 (clk_e, clk, counter_2_q);
  and and_1 (clk_s, clk, counter_2_q);
endmodule

module stepper (
  input  clk,
  input  rst,
  output _1,
  output _2,
  output _3,
  output _4,
  output _5,
  output _6,
  output _0
);

  wire d_ff_1_q, d_ff_2_q, d_ff_3_q, d_ff_4_q, d_ff_5_q, d_ff_6_q, not_1_out, not_2_out, not_3_out,
       not_4_out, not_5_out, not_6_out, not_7_out;

  or or_1 (_0, rst, not_2_out);
  not not_1 (not_1_out, rst);
  not not_2 (not_2_out, d_ff_3_q);
  D_Flip_Flop d_ff_1 (.clk(clk), .D(not_1_out), .Q(d_ff_1_q), .reset(rst));  // open: Qn, preset, en
  and and_1 (_1, d_ff_3_q, not_3_out);
  not not_3 (not_3_out, d_ff_2_q);
  D_Flip_Flop d_ff_2 (.clk(clk), .D(d_ff_3_q), .Q(d_ff_2_q), .reset(rst));  // open: Qn, preset, en
  D_Flip_Flop d_ff_3 (.clk(clk), .D(d_ff_1_q), .Q(d_ff_3_q), .reset(rst));  // open: Qn, preset, en
  and and_2 (_2, d_ff_2_q, not_4_out);
  not not_4 (not_4_out, d_ff_4_q);
  D_Flip_Flop d_ff_4 (.clk(clk), .D(d_ff_2_q), .Q(d_ff_4_q), .reset(rst));  // open: Qn, preset, en
  and and_3 (_3, d_ff_4_q, not_5_out);
  not not_5 (not_5_out, d_ff_5_q);
  D_Flip_Flop d_ff_5 (.clk(clk), .D(d_ff_4_q), .Q(d_ff_5_q), .reset(rst));  // open: Qn, preset, en
  and and_4 (_4, d_ff_5_q, not_6_out);
  not not_6 (not_6_out, d_ff_6_q);
  D_Flip_Flop d_ff_6 (.clk(clk), .D(d_ff_5_q), .Q(d_ff_6_q), .reset(rst));  // open: Qn, preset, en
  and and_5 (_5, d_ff_6_q, not_7_out);
  not not_7 (not_7_out, _6);
  D_Flip_Flop d_ff_7 (.clk(clk), .D(d_ff_6_q), .Q(_6), .reset(rst));  // open: Qn, preset, en
endmodule

module control_circuit (
  input  [7:0] IR,
  output _8MAR,
  output RAM,
  output _16MAR,
  output ACC,
  output ACC_2,
  output RSET,
  output RAM_2,
  output IAR0,
  output TMP,
  output IAR1,
  output REN,
  output bus1,
  output IR_2,
  output CNTR_plus_plus,
  output IAR0_2,
  output CNTR_TMP_0,
  output IAR1_2,
  output CNTR_TMP_0_2,
  output CNTR,
  output CNTR_TMP0,
  output [1:0] RSEL_A,
  output [1:0] RSEL_B,
  output CNTR_TMP1,
  output [1:0] RSET_B,
  output [2:0] OP
);

  wire _1__0, _1__1, _1__2, _1__3, _1__4, _1__5, _1__6, _1__7, _1__8, _1__9, and_10_out, and_11_out,
       and_12_out, and_13_out, and_14_out, and_15_out, and_16_out, clock_1_clk, clock_1_clk_e, clock_1_clk_s,
       clock_2_out, not_1_out, not_2_out, or_1_out, or_2_out, or_3_out, or_4_out, or_5_out, or_6_out,
       or_7_out, or_8_out, or_9_out, or_10_out, or_11_out, or_12_out, or_13_out, or_14_out, or_15_out,
       or_16_out, or_17_out, or_18_out, or_19_out, or_20_out, or_21_out;

  clock clock_1 (.in_1(clock_2_out), .clk(clock_1_clk), .clk_e(clock_1_clk_e), .clk_s(clock_1_clk_s));
  Clock clock_2 (.out(clock_2_out));
  and and_1 (RAM, clock_1_clk_e, or_1_out);
  and and_2 (ACC, clock_1_clk_e, or_2_out);
  and and_3 (RSET, clock_1_clk_e, or_3_out);
  and and_4 (IAR0, clock_1_clk_e, or_4_out);
  and and_5 (IAR1, clock_1_clk_e, or_5_out);
  and and_6 (bus1, clock_1_clk_e, or_6_out);
  and and_7 (CNTR_plus_plus, clock_1_clk_e, or_7_out);
  and and_8 (CNTR_TMP_0, clock_1_clk_e, or_8_out);
  and and_9 (CNTR_TMP_0_2, clock_1_clk_e, or_9_out);
  and and_10 (and_10_out, and_15_out, clock_1_clk_e);
  and and_11 (and_11_out, and_14_out, clock_1_clk_e);
  assign RSEL_A = and_11_out ? IR[3:2] : 2'bz;  // Controlled_Buffer controlled_buffer_1
  assign RSEL_B = and_10_out ? IR[1:0] : 2'bz;  // Controlled_Buffer controlled_buffer_2
  buf or_1 (or_1_out, _1__5);  // OR_Gate
  buf or_2 (or_2_out, and_16_out);  // OR_Gate
  // OR_Gate or_3 has open pins: out=or_3_out
  buf or_4 (or_4_out, _1__0);  // OR_Gate
  buf or_5 (or_5_out, _1__1);  // OR_Gate
  // OR_Gate or_6 has open pins: out=or_6_out
  buf or_7 (or_7_out, _1__2);  // OR_Gate
  buf or_8 (or_8_out, _1__3);  // OR_Gate
  buf or_9 (or_9_out, _1__4);  // OR_Gate
  not not_1 (not_1_out, IR[7]);
  and and_12 (and_12_out, IR[6], IR[5], IR[4]);
  not not_2 (not_2_out, and_12_out);
  Decoder #(.select(3)) decoder_1 (
    .sel(IR[6:4]), .en(not_1_out));  // open: out0, out1, out2, out3, out4, out5, out6, out7
  and and_13 (and_13_out, and_16_out, clock_1_clk_s);
  assign RSET_B = and_13_out ? IR[1:0] : 2'bz;  // Controlled_Buffer controlled_buffer_3
  and and_14 (and_14_out, _1__7, IR[7]);
  and and_15 (and_15_out, _1__6, IR[7]);
  and and_16 (and_16_out, _1__8, not_2_out, IR[7]);
  stepper9 _1 (
    .clk(clock_1_clk), .rst(_1__9), ._0(_1__0), ._1(_1__1), ._2(_1__2), ._3(_1__3), ._4(_1__4), ._5(_1__5),
    ._6(_1__6), ._7(_1__7), ._8(_1__8), ._9(_1__9));
  buf or_10 (or_10_out, _1__0);  // OR_Gate
  buf or_11 (or_11_out, _1__1);  // OR_Gate
  buf or_12 (or_12_out, and_14_out);  // OR_Gate
  // OR_Gate or_13 has open pins: out=or_13_out
  buf or_14 (or_14_out, and_15_out);  // OR_Gate
  // OR_Gate or_15 has open pins: out=or_15_out
  buf or_16 (or_16_out, _1__5);  // OR_Gate
  buf or_17 (or_17_out, _1__3);  // OR_Gate
  buf or_18 (or_18_out, _1__4);  // OR_Gate
  buf or_19 (or_19_out, _1__1);  // OR_Gate
  buf or_20 (or_20_out, _1__2);  // OR_Gate
  buf or_21 (or_21_out, _1__2);  // OR_Gate
  and and_17 (_8MAR, clock_1_clk_s, or_10_out);
  and and_18 (_16MAR, clock_1_clk_s, or_11_out);
  and and_19 (ACC_2, clock_1_clk_s, or_12_out);
  and and_20 (RAM_2, clock_1_clk_s, or_13_out);
  and and_21 (TMP, clock_1_clk_s, or_14_out);
  and and_22 (REN, clock_1_clk_s, or_15_out);
  and and_23 (IR_2, clock_1_clk_s, or_16_out);
  and and_24 (IAR0_2, clock_1_clk_s, or_17_out);
  and and_25 (IAR1_2, clock_1_clk_s, or_18_out);
  and and_26 (CNTR, clock_1_clk_s, or_19_out);
  and and_27 (CNTR_TMP0, clock_1_clk_s, or_20_out);
  and and_28 (CNTR_TMP1, clock_1_clk_s, or_21_out);

  assign OP = IR[6:4];

  // Notes on the sheet:
  //   ENABLES
  //   REGB
  //   REGA
  //   2
  //   1
  //   4
  //   5
  //   3
  //   8
  //   7
  //   6
  //   9
  //   SETS
endmodule

module bus1 (
  input  [7:0] BUSI,
  input  OP,
  output [7:0] BUSO
);

  wire not_1_out;

  and and_1 (BUSO[6], BUSI[6], not_1_out);
  and and_2 (BUSO[7], BUSI[7], not_1_out);
  and and_3 (BUSO[5], BUSI[5], not_1_out);
  and and_4 (BUSO[4], BUSI[4], not_1_out);
  and and_5 (BUSO[2], BUSI[2], not_1_out);
  and and_6 (BUSO[1], BUSI[1], not_1_out);
  and and_7 (BUSO[3], BUSI[3], not_1_out);
  not not_1 (not_1_out, OP);
  or or_1 (BUSO[0], BUSI[0], OP);
endmodule

module stepper8 (
  input  clk,
  input  rst,
  output _1,
  output _2,
  output _3,
  output _4,
  output _5,
  output _0,
  output _6,
  output _7,
  output _8
);

  wire d_ff_1_q, d_ff_2_q, d_ff_3_q, d_ff_4_q, d_ff_5_q, d_ff_6_q, d_ff_7_q, not_1_out, not_2_out, not_3_out,
       not_4_out, not_5_out, not_6_out, not_7_out, not_8_out, not_9_out;

  or or_1 (_0, rst, not_1_out);
  not not_1 (not_1_out, d_ff_1_q);
  not not_2 (not_2_out, rst);
  and and_1 (_1, d_ff_1_q, not_4_out);
  D_Flip_Flop d_ff_1 (.clk(clk), .D(not_2_out), .Q(d_ff_1_q), .reset(rst));  // open: Qn, preset, en
  and and_2 (_2, d_ff_2_q, not_3_out);
  not not_3 (not_3_out, d_ff_3_q);
  not not_4 (not_4_out, d_ff_2_q);
  D_Flip_Flop d_ff_2 (.clk(clk), .D(d_ff_1_q), .Q(d_ff_2_q), .reset(rst));  // open: Qn, preset, en
  and and_3 (_3, d_ff_3_q, not_5_out);
  not not_5 (not_5_out, d_ff_4_q);
  D_Flip_Flop d_ff_3 (.clk(clk), .D(d_ff_2_q), .Q(d_ff_3_q), .reset(rst));  // open: Qn, preset, en
  D_Flip_Flop d_ff_4 (.clk(clk), .D(d_ff_3_q), .Q(d_ff_4_q), .reset(rst));  // open: Qn, preset, en
  and and_4 (_4, d_ff_4_q, not_6_out);
  not not_6 (not_6_out, d_ff_5_q);
  D_Flip_Flop d_ff_5 (.clk(clk), .D(d_ff_4_q), .Q(d_ff_5_q), .reset(rst));  // open: Qn, preset, en
  and and_5 (_5, d_ff_5_q, not_7_out);
  not not_7 (not_7_out, d_ff_6_q);
  D_Flip_Flop d_ff_6 (.clk(clk), .D(d_ff_5_q), .Q(d_ff_6_q), .reset(rst));  // open: Qn, preset, en
  and and_6 (_6, d_ff_6_q, not_8_out);
  not not_8 (not_8_out, d_ff_7_q);
  D_Flip_Flop d_ff_7 (.clk(clk), .D(d_ff_6_q), .Q(d_ff_7_q), .reset(rst));  // open: Qn, preset, en
  and and_7 (_7, d_ff_7_q, not_9_out);
  not not_9 (not_9_out, _8);
  D_Flip_Flop d_ff_8 (.clk(clk), .D(d_ff_7_q), .Q(_8), .reset(rst));  // open: Qn, preset, en
endmodule

module ccircuitwrapper16 (
  input  [7:0] IR,
  output [1:0] ACC0,
  output SET_8_MAR,
  output SET_16_MAR,
  output SET_RAM,
  output SET_TMP,
  output [1:0] RSEL_B,
  output [1:0] RS_E,
  output [1:0] RSEL_A,
  output BUS_1,
  output [1:0] IAR0,
  output [1:0] out_12,
  output [1:0] IAR1,
  output [1:0] out_14,
  output SET_ALU_ACC1,
  output [1:0] out_16,
  output SET_IR,
  output EN_RAM,
  output [2:0] SET_OP
);

  // control_circuit control_circuit_1: pin names not known; wires that end beside it: RSEL_B, RSEL_A, out_12[0], out_12[1], out_14[0], out_14[1], out_16[0], out_16[1], ACC0[1], ACC0[0], SET_8_MAR, SET_16_MAR, SET_RAM, SET_TMP, RS_E[0], RS_E[1], BUS_1, IAR0[0], IAR0[1], IAR1[0], IAR1[1], SET_ALU_ACC1, SET_IR, EN_RAM, SET_OP
endmodule

module _16_mem_test (
  input  [15:0] in_1,
  input  in_2,
  input  in_3,
  input  in_4,
  input  in_5,
  input  [7:0] in_6,
  input  in_7,
  input  [7:0] in_8,
  input  in_9,
  input  in_10,
  input  in_11,
  input  zero
);

  wire and_1_out, and_2_out, and_3_out, and_4_out, and_5_out, and_6_out, clock_1_out, clock_2_p2, clock_2_p3,
       clock_2_p4, or_1_out, stepper_1__0, stepper_1__1, stepper_1__2, stepper_1__6;
  wire [7:0] register_2_q, register_3_q, register_7_q, register_8_q, shift_register_1_out,
       shift_register_2_q0, shift_register_2_q1;
  wire [15:0] counter_1_q, register_1_q, register_5_q;

  Clock clock_1 (.out(clock_1_out));
  // clock clock_2: pin names not known; wires that end beside it: clock_1_out, clock_2_p2, clock_2_p3, clock_2_p4
  Register #(.width(16)) register_1 (.D(in_1), .Q(register_1_q), .clk(in_2));  // open: en, clr
  Shift_Register #(.width(8), .length(2)) shift_register_1 (
    .clk(in_4), .out(shift_register_1_out), .load(in_3), .d0(register_1_q[15:8]), .d1(register_1_q[7:0]));  // open: shift, in, clr, q0, q1
  // Probe on register_1_q[15:8]
  // Probe on register_1_q[7:0]
  stepper stepper_1 (
    .clk(clock_2_p2), .rst(stepper_1__6), ._0(stepper_1__0), ._1(stepper_1__1), ._2(stepper_1__2),
    ._6(stepper_1__6));  // open: _3, _4, _5
  and and_1 (and_1_out, stepper_1__1, clock_2_p3);
  and and_2 (and_2_out, stepper_1__0, clock_2_p3);
  Shift_Register #(.width(8), .length(2)) shift_register_2 (
    .in(shift_register_1_out), .clk(in_4), .q0(shift_register_2_q0), .q1(shift_register_2_q1));  // open: shift, out, load, clr, d0, d1
  // Probe on register_5_q[15:8]
  Register register_2 (.D(in_6), .Q(register_2_q), .clk(in_7), .clr(zero));  // open: en
  assign register_5_q[15:8] = and_1_out ? register_2_q : 8'bz;  // Controlled_Buffer controlled_buffer_1
  // Probe on register_5_q[15:8]
  Register register_3 (.D(in_8), .Q(register_3_q), .clk(in_9), .clr(zero));  // open: en
  assign register_5_q[15:8] = and_2_out ? register_3_q : 8'bz;  // Controlled_Buffer controlled_buffer_2
  // Probe on shift_register_2_q1
  // Probe on shift_register_2_q0
  Register #(.width(16)) register_4 (.D({shift_register_2_q0, shift_register_2_q1}), .clk(in_5));  // open: en, Q, clr
  Register register_5 (.D(register_5_q[15:8]), .Q(register_5_q[7:0]), .clk(and_3_out), .clr(zero));  // open: en
  and and_3 (and_3_out, stepper_1__0, clock_2_p4);
  and and_4 (and_4_out, stepper_1__1, clock_2_p4);
  // Probe on register_5_q
  or or_1 (or_1_out, and_4_out, and_5_out);
  and and_5 (and_5_out, stepper_1__2, clock_2_p3);
  Register #(.width(16)) register_6 (.D(register_5_q), .clk(and_4_out), .clr(zero));  // open: en, Q
  Register register_7 (.D(counter_1_q[7:0]), .Q(register_7_q), .clk(and_6_out), .clr(zero));  // open: en
  Counter #(.width(16), .max('hffff)) counter_1 (
    .load(and_4_out), .D(register_5_q), .count(and_5_out), .Q(counter_1_q), .clk(or_1_out), .clr(zero));  // open: carry
  Register register_8 (.D(counter_1_q[15:8]), .Q(register_8_q), .clk(and_6_out), .clr(zero));  // open: en
  and and_6 (and_6_out, stepper_1__2, clock_2_p4);
  Controlled_Buffer #(.width(8)) controlled_buffer_3 (.in(register_7_q), .en(in_11));  // open: out
  Controlled_Buffer #(.width(8)) controlled_buffer_4 (.in(register_8_q), .en(in_10));  // open: out
endmodule

module _16registre (
  input  [15:0] I,
  input  in_2,
  input  [1:0] s_e,
  output [15:0] out_4,
  output [15:0] O
);

  Register #(.width(16)) register_1 (.D(I), .Q(out_4), .clk(s_e[1]), .clr(in_2));  // open: en
  assign O = s_e[0] ? out_4 : 16'bz;  // Controlled_Buffer controlled_buffer_1
  Pull_Resistor pull_resistor_1 (.node(s_e[0]));
endmodule

module stepper9 (
  input  clk,
  input  rst,
  output _1,
  output _2,
  output _3,
  output _4,
  output _5,
  output _0,
  output _6,
  output _7,
  output _8,
  output _9
);

  wire d_ff_1_q, d_ff_2_q, d_ff_3_q, d_ff_4_q, d_ff_5_q, d_ff_6_q, d_ff_7_q, d_ff_8_q, not_1_out, not_2_out,
       not_3_out, not_4_out, not_5_out, not_6_out, not_7_out, not_8_out, not_9_out, not_10_out;

  or or_1 (_0, rst, not_1_out);
  not not_1 (not_1_out, d_ff_1_q);
  not not_2 (not_2_out, rst);
  and and_1 (_1, d_ff_1_q, not_4_out);
  D_Flip_Flop d_ff_1 (.clk(clk), .D(not_2_out), .Q(d_ff_1_q), .reset(rst));  // open: Qn, preset, en
  and and_2 (_2, d_ff_2_q, not_3_out);
  not not_3 (not_3_out, d_ff_4_q);
  not not_4 (not_4_out, d_ff_2_q);
  D_Flip_Flop d_ff_2 (.clk(clk), .D(d_ff_1_q), .Q(d_ff_2_q), .reset(rst));  // open: Qn, preset, en
  and and_3 (_3, d_ff_4_q, not_5_out);
  not not_5 (not_5_out, d_ff_3_q);
  D_Flip_Flop d_ff_3 (.clk(clk), .D(d_ff_4_q), .Q(d_ff_3_q), .reset(rst));  // open: Qn, preset, en
  D_Flip_Flop d_ff_4 (.clk(clk), .D(d_ff_2_q), .Q(d_ff_4_q), .reset(rst));  // open: Qn, preset, en
  and and_4 (_4, d_ff_3_q, not_6_out);
  not not_6 (not_6_out, d_ff_5_q);
  D_Flip_Flop d_ff_5 (.clk(clk), .D(d_ff_3_q), .Q(d_ff_5_q), .reset(rst));  // open: Qn, preset, en
  and and_5 (_5, d_ff_5_q, not_7_out);
  not not_7 (not_7_out, d_ff_6_q);
  D_Flip_Flop d_ff_6 (.clk(clk), .D(d_ff_5_q), .Q(d_ff_6_q), .reset(rst));  // open: Qn, preset, en
  and and_6 (_6, d_ff_6_q, not_8_out);
  not not_8 (not_8_out, d_ff_7_q);
  D_Flip_Flop d_ff_7 (.clk(clk), .D(d_ff_6_q), .Q(d_ff_7_q), .reset(rst));  // open: Qn, preset, en
  and and_7 (_8, d_ff_8_q, not_10_out);
  and and_8 (_7, d_ff_7_q, not_9_out);
  not not_9 (not_9_out, d_ff_8_q);
  not not_10 (not_10_out, _9);
  D_Flip_Flop d_ff_8 (.clk(clk), .D(d_ff_7_q), .Q(d_ff_8_q), .reset(rst));  // open: Qn, preset, en
  D_Flip_Flop d_ff_9 (.clk(clk), .D(d_ff_8_q), .Q(_9), .reset(rst));  // open: Qn, preset, en
endmodule

module _8CC (
  input  CLK_IN,
  input  [7:0] IR,
  input  [3:0] FLAGS,
  output bus1,
  output MAR,
  output RAM,
  output ACC,
  output ACC_2,
  output RAM_2,
  output IAR,
  output TMP,
  output R0,
  output IR_2,
  output R1,
  output R2,
  output IAR_2,
  output R3,
  output R0_2,
  output R1_2,
  output R2_2,
  output R3_2,
  output FLAGS_2,
  output [2:0] OP_CODE
);

  wire _1, _2, _3, _4, _4_0, _4_1, _4_2, _4_3, _4_4, _4_5, _4_6, _4_8, _5, _5_0, _5_1, _5_2, _5_4, _5_5,
       _5_8, _6, _6_2, _6_5, _6_8, and_5_out, and_6_out, and_7_out, and_8_out, and_9_out, and_10_out,
       and_11_out, and_12_out, and_13_out, and_16_out, and_18_out, and_19_out, and_20_out, and_21_out,
       clock_1_clk, clock_1_clk_e, clock_1_clk_s, decoder_1_out0, decoder_1_out1, decoder_1_out2,
       decoder_1_out3, decoder_2_out0, decoder_2_out1, decoder_2_out2, decoder_2_out3, decoder_3_out0,
       decoder_3_out1, decoder_3_out2, decoder_3_out3, decoder_3_out4, decoder_3_out5, decoder_3_out6,
       decoder_4_out0, decoder_4_out1, decoder_4_out2, decoder_4_out3, not_1_out, not_2_out, or_5_out,
       or_6_out, or_7_out, or_8_out, or_9_out, or_10_out, or_11_out, or_12_out, or_13_out, or_14_out,
       or_15_out, or_16_out, or_17_out, or_18_out, or_19_out, stepper_1__6;

  or or_1 (R0, and_5_out, and_9_out);
  or or_2 (R1, and_6_out, and_10_out);
  or or_3 (R2, and_7_out, and_11_out);
  or or_4 (R3, and_8_out, and_12_out);
  clock clock_1 (.in_1(CLK_IN), .clk(clock_1_clk), .clk_e(clock_1_clk_e), .clk_s(clock_1_clk_s));
  and and_1 (bus1, or_5_out, clock_1_clk_e);
  and and_2 (RAM, clock_1_clk_e, or_6_out);
  and and_3 (ACC_2, or_7_out, clock_1_clk_e);
  and and_4 (IAR, clock_1_clk_e, or_8_out);
  and and_5 (and_5_out, clock_1_clk_e, or_9_out, decoder_1_out0);
  and and_6 (and_6_out, clock_1_clk_e, or_9_out, decoder_1_out1);
  and and_7 (and_7_out, clock_1_clk_e, or_9_out, decoder_1_out2);
  and and_8 (and_8_out, clock_1_clk_e, or_9_out, decoder_1_out3);
  and and_9 (and_9_out, clock_1_clk_e, or_10_out, decoder_2_out0);
  and and_10 (and_10_out, clock_1_clk_e, or_10_out, decoder_2_out1);
  and and_11 (and_11_out, clock_1_clk_e, or_10_out, decoder_2_out2);
  and and_12 (and_12_out, clock_1_clk_e, or_10_out, decoder_2_out3);
  Pull_Resistor pull_resistor_1 (.node(OP_CODE));
  or or_5 (or_5_out, _1, _4_2, _4_5, _4_6);
  or or_6 (or_6_out, _2, _5_0, _5_2, _5_4, _6_5);
  or or_7 (or_7_out, _3, _6_8, _6_2, _5_5);
  or or_8 (or_8_out, _1, _4_2, _4_4, _4_5);
  or or_9 (or_9_out, _5_1, _4_3, _4_8);
  Decoder #(.select(2)) decoder_1 (
    .out0(decoder_1_out0), .out1(decoder_1_out1), .out2(decoder_1_out2), .out3(decoder_1_out3), .sel(IR[1:0]));  // open: en
  Decoder #(.select(2)) decoder_2 (
    .out0(decoder_2_out0), .out1(decoder_2_out1), .out2(decoder_2_out2), .out3(decoder_2_out3), .sel(IR[3:2]));  // open: en
  or or_10 (or_10_out, _4_0, _4_1, _5_8);
  and and_13 (and_13_out, _5, IR[7]);
  assign OP_CODE = and_13_out ? IR[6:4] : 3'bz;  // Controlled_Buffer controlled_buffer_1
  and and_14 (_5_8, _5, IR[7]);
  and and_15 (_4_8, _4, IR[7]);
  not not_1 (not_1_out, and_16_out);
  and and_16 (and_16_out, IR[6], IR[5], IR[4]);
  and and_17 (_6_8, _6, not_1_out, IR[7]);
  and and_18 (and_18_out, IR[0], FLAGS[0]);
  and and_19 (and_19_out, IR[1], FLAGS[1]);
  and and_20 (and_20_out, IR[2], FLAGS[2]);
  and and_21 (and_21_out, IR[3], FLAGS[3]);
  stepper stepper_1 (
    .clk(clock_1_clk), .rst(stepper_1__6), ._0(_1), ._1(_2), ._2(_3), ._3(_4), ._4(_5), ._5(_6),
    ._6(stepper_1__6));
  or or_11 (or_11_out, _1, _4_0, _4_1, _4_2, _4_4, _4_5);
  or or_12 (or_12_out, _1, _5_8, _4_2, _4_5);
  buf or_13 (or_13_out, _5_1);  // OR_Gate
  buf or_14 (or_14_out, _4_8);  // OR_Gate
  buf or_15 (or_15_out, _2);  // OR_Gate
  or or_16 (or_16_out, _3, _6_2, _4_3, _5_4, _5_5, _6_5);
  or or_17 (or_17_out, _5_8, _4_6);
  Decoder #(.select(3), .disabled(0)) decoder_3 (
    .out0(decoder_3_out0), .out1(decoder_3_out1), .out2(decoder_3_out2), .out3(decoder_3_out3),
    .out4(decoder_3_out4), .out5(decoder_3_out5), .out6(decoder_3_out6), .sel(IR[6:4]), .en(not_2_out));  // open: out7
  not not_2 (not_2_out, IR[7]);
  or or_18 (or_18_out, and_18_out, and_19_out, and_20_out, and_21_out);
  and and_22 (MAR, or_11_out, clock_1_clk_s);
  and and_23 (ACC, clock_1_clk_s, or_12_out);
  and and_24 (RAM_2, or_13_out, clock_1_clk_s);
  and and_25 (TMP, clock_1_clk_s, or_14_out);
  and and_26 (IR_2, or_15_out, clock_1_clk_s);
  and and_27 (IAR_2, clock_1_clk_s, or_16_out);
  and and_28 (FLAGS_2, clock_1_clk_s, or_17_out);
  or or_19 (or_19_out, _6_8, _5_2, _5_0);
  Decoder #(.select(2)) decoder_4 (
    .out0(decoder_4_out0), .out1(decoder_4_out1), .out2(decoder_4_out2), .out3(decoder_4_out3), .sel(IR[1:0]));  // open: en
  and and_29 (R0_2, or_19_out, decoder_4_out0, clock_1_clk_s);
  and and_30 (R1_2, or_19_out, decoder_4_out1, clock_1_clk_s);
  and and_31 (R2_2, or_19_out, decoder_4_out2, clock_1_clk_s);
  and and_32 (R3_2, or_19_out, decoder_4_out3, clock_1_clk_s);
  and and_33 (_4_6, decoder_3_out6, _4);
  and and_34 (_4_5, decoder_3_out5, _4);
  and and_35 (_5_5, decoder_3_out5, _5);
  and and_36 (_6_5, or_18_out, decoder_3_out5, _6);
  and and_37 (_4_4, decoder_3_out4, _4);
  and and_38 (_5_4, decoder_3_out4, _5);
  and and_39 (_4_3, decoder_3_out3, _4);
  and and_40 (_4_2, decoder_3_out2, _4);
  and and_41 (_5_2, decoder_3_out2, _5);
  and and_42 (_6_2, decoder_3_out2, _6);
  and and_43 (_4_1, decoder_3_out1, _4);
  and and_44 (_5_1, decoder_3_out1, _5);
  and and_45 (_4_0, decoder_3_out0, _4);
  and and_46 (_5_0, decoder_3_out0, _5);

  // Notes on the sheet:
  //   s
  //   e
  //   E
  //   g
  //   0
  //   E
  //   c
  //   B
  //   A
  //   S
  //   S B
endmodule
